# Fritzing sketch tangelo_prototype (saved by Fritzing 1.0.5)
breadboards: 1

parts:
  LSM6DSOX1 = Adafruit LSM6DSOX
  S1 = Toggle Switch [package=THT]
  S2 = Pushbutton [package="[THT]"]
  Part2 = Adafruit HUZZAH32 ESP32 Feather [part_number="Adafruit #3405"]
  R1 = Resistor [tolerance=±5% power=0.25W resistance=330 package=THT]
  R2 = Resistor [tolerance=±5% power=0.25W resistance=330 package=THT]
  R3 = Resistor [tolerance=±5% power=0.25W resistance=330 package=THT]

nets:
  VCC: LSM6DSOX1.VCC, S1.COM, S2.Pin_3, S2.Pin_4, Part2.3.3V
  GND: LSM6DSOX1.GND, Part2.GND, R1.Pin_1, R2.Pin_1, R3.Pin_1
  N1: LSM6DSOX1.SCL, Part2.MISO
  N2: LSM6DSOX1.SDA, Part2.IO16
  N3: LSM6DSOX1.SDO, Part2.IO17
  N4: LSM6DSOX1.CS_5V, Part2.SDA
  N5: S1.L1, Part2.IO15_A8, R1.Pin_0
  N6: S1.L2, Part2.IO33_A9, R2.Pin_0
  N7: S2.Pin_1, S2.Pin_2, Part2.IO32_A7, R3.Pin_0
